// Digital circuit execute.dig as structural Verilog
module execute (
  input  [15:0] L,
  input  [15:0] R,
  input  [2:0] cond,
  input  [2:0] op,
  output [15:0] L_out,
  output [15:0] result,
  output skip_n
);

  wire and_1_out, and_3_out, and_4_out, C, eq, ge, hs, lt, N, ne, RN, V;
  wire [14:0] add_1_s, multiplexer_1_out;
  wire [15:0] and_2_out, not_1_out, or_1_out, \xor ;

  assign not_1_out = ~R;  // Not not_1, 16 bits wide
  Multiplexer #(.Bits(16)) multiplexer_1 (.sel(and_1_out), .in_0(R), .in_1(not_1_out), .out({RN, multiplexer_1_out}));
  and and_1 (and_1_out, op[1], ~op[2]);  // And
  Add #(.Bits(16)) add_1 (.a(L), .b({RN, multiplexer_1_out}), .c_i(and_1_out), .s({N, add_1_s}), .c_o(C));
  assign \xor  = L ^ R;  // XOr xor_1, 16 bits wide
  assign and_2_out = L & R;  // And and_2, 16 bits wide
  assign or_1_out = L | R;  // Or or_1, 16 bits wide
  Multiplexer #(.Selector_Bits(3), .Bits(16)) multiplexer_2 (
    .sel(op), .in_0({16{1'b0}}), .in_1({N, add_1_s}), .in_2({N, add_1_s}), .in_3({16{1'b0}}), .in_4(R),
    .in_5(\xor ), .in_6(and_2_out), .in_7(or_1_out), .out(result));
  xor xor_2 (ge, N, V);
  Comparator #(.Bits(16)) u_eq (.a(\xor ), .b({16{1'b0}}), .eq(ne));  // open: gt, lt
  and and_3 (and_3_out, L[15], RN, ~N);  // And
  and and_4 (and_4_out, ~L[15], ~RN, N);  // And
  not not_2 (lt, ge);
  not not_3 (hs, C);
  not not_4 (eq, ne);
  or or_2 (V, and_3_out, and_4_out);
  Multiplexer #(.Selector_Bits(3)) multiplexer_3 (
    .sel(cond), .in_0(1'b0), .in_1(eq), .in_2(ne), .in_3(lt), .in_4(ge), .in_5(C), .in_6(hs), .in_7(1'b0),
    .out(skip_n));

  assign L_out = L;

  // Other names for the same wires on the sheet: LN = L[15]; lo = C
endmodule
