// Digital circuit fetch.dig as structural Verilog
module fetch (
  input  [15:0] instr_i,
  input  clock,
  input  en,
  input  jump,
  input  [15:0] value,
  output [3:0] pc,
  output [15:0] instr_o
);

  wire and_1_out;

  and and_1 (and_1_out, en, jump);
  CounterPreset #(.Bits(4), .isProgramCounter("true")) u_PC (
    .en(en), .C(clock), .dir(1'b0), .in(value[3:0]), .ld(and_1_out), .clr(1'b0), .out(pc));  // open: ovf

  assign instr_o = instr_i;
endmodule
