// Digital circuit rj32.dig as structural Verilog
module rj32 (
  input  clock,
  input  step,
  input  run_slow,
  input  [15:0] D_prog,
  input  [15:0] D_in,
  input  run_fast,
  input  run_faster,
  input  erun,
  output halt,
  output error,
  output skip,
  output stall,
  output [7:0] A_prog,
  output clock_m,
  output [13:0] A_data,
  output [15:0] D_out,
  output w_en,
  output [25:0] db
);

  wire decoder_1_p2, fetch_1_p7, skip_n;
  wire [2:0] aluop_t, cond_t;
  wire [12:0] decode_t;
  wire [15:0] decoder_1_p1, imm_t, L_t, R_t, result_t, wrval_t;
  wire [15:4] ctrl_t;
  wire [15:8] A_prog_t;

  not not_1 (clock_m, clock);
  // fetch fetch_1: pin names not known; wires that end beside it: result_t, D_prog, clock, ctrl_t[11], ctrl_t[4], ctrl_t[12], fetch_1_p7, {A_prog_t, A_prog}
  // decoder decoder_1: pin names not known; wires that end beside it: decoder_1_p1, decoder_1_p2, fetch_1_p7, {A_prog_t, A_prog}, ctrl_t[4], decode_t[7:4], decode_t[3:0], L_t, R_t, cond_t, decode_t[12:8], ctrl_t[14], ctrl_t[13], imm_t, ctrl_t[15]
  clockctrl clockctrl_1 (
    .clock(clock), .step(step), .slow(run_slow), .fast(run_fast), .faster(run_faster), .efast(erun),
    .stall(stall));
  // control control_1: pin names not known; wires that end beside it: decode_t[12:8], stall, clock, skip_n, aluop_t, skip, halt, error, ctrl_t[12], ctrl_t[8], ctrl_t[9], ctrl_t[11], ctrl_t[4], ctrl_t[10]
  // execute execute_1: pin names not known; wires that end beside it: L_t, R_t, cond_t, aluop_t, result_t, skip_n
  memaccess memaccess_1 (
    .result(result_t), .rdval(decoder_1_p1), .mem(ctrl_t[8]), .memop(ctrl_t[9]), .D(D_in), .en(ctrl_t[12]),
    .wrval(wrval_t), .A(A_data), .str(w_en), .D_in(D_out));
  debugbus debugbus_1 (
    .db_ready(1'b1), .clock(clock), .ctrl({ctrl_t[15:8], aluop_t, ctrl_t[4], error, halt, skip, stall}),
    .decode({cond_t, decode_t}), .wrval(wrval_t), .result(result_t), .L(L_t), .R(R_t), .imm(imm_t),
    .pc({A_prog_t, A_prog}), .db(db));
  // regfile regfile_1: pin names not known; wires that end beside it: decode_t[7:4], decode_t[3:0], wrval_t, clock, ctrl_t[12], ctrl_t[10], decoder_1_p1, decoder_1_p2

  // Other names for the same wires on the sheet: A_data_t[13:0] = A_data;
  //   ctrl_t (some bits) = {aluop_t, error, halt, skip, stall}; C = clock; decode_t[15:13] = cond_t;
  //   D_in_t[15:0] = D_in; D_out_t[15:0] = D_out; D_prog_t[15:0] = D_prog; en = ctrl_t[12]; en_fetch = ctrl_t[11];
  //   error_t = error; halt_t = halt; immv_t = ctrl_t[15]; jump_t = ctrl_t[4]; mem_t = ctrl_t[8];
  //   op_t[4:0] = decode_t[12:8]; A_prog_t[7:0] = A_prog; PC_t[15:0] = {A_prog_t, A_prog}; rd_t[3:0] = decode_t[3:0];
  //   rdvalid_t = ctrl_t[13]; rs_t[3:0] = decode_t[7:4]; rsvalid_t = ctrl_t[14]; skip_t = skip; stall_t = stall;
  //   store_t = ctrl_t[9]; W_en_t = w_en; write_t = ctrl_t[10]

  // Notes on the sheet:
  //   clock: Hz: 10
  //   rj45 Creates
endmodule
