// Digital circuit testsuite.dig as structural Verilog
module testsuite (
  input  clock,
  input  run,
  output error,
  output halt,
  output [7:0] PC
);

  frontpanel frontpanel_1 (.clock(clock), .erun(run), .PC(PC), .halt(halt), .error(error));  // open: DC, R0, R1, R2, R3
endmodule

/* Test case add:
clock run error halt

# #include "../cpudef.asm"
# 
# move r1, 5
# move r2, 3
# add r1, r2
# add r1, 2
# if.ne r1, 10
# error
# halt

program(0x1171, 0x20f1, 0x1280, 0x1081, 0x1523, 0x0010, 0x0018)

let i = 0;
while(!(halt | error | (i >= 100)))
  let i = i + 1;
  0 1 0 0
  1 1 x x
end while
0 1 0 1
*/

/* Test case jump:
clock run error halt

# #include "../cpudef.asm"
# 
#   jump one
#   halt
# three:
#   add r0, r1
#   add r0, r2
#   jump end
#   halt
# two:
#   move r2, 2
#   jump three
#   halt
# one:
#   move r1, 3
#   jump two
#   halt
# end:
#   if.ne r0, 5
#   error
#   halt

program(0x0095, 0x0018, 0x0180, 0x0280, 0x00c5, 0x0018, 0x20b1, 0x0025, 0x0018, 0x10f1, 0x0065, 0x0018, 0x02a3, 0x0010, 0x0018)

let i = 0;
while(!(halt | error | (i >= 100)))
  let i = i + 1;
  0 1 0 0
  1 1 x x
end while
0 1 0 1
*/

/* Test case if.eq:
clock run error halt

# #include "../cpudef.asm"
# 
# move r1, 2
# move r2, 3
# move r3, 3
# 
# ; skip r-r
# if.eq r1, r2
# error
# 
# ; skip r-i
# if.eq r1, 3
# error
# 
# ; no-skip r-r
# if.eq r2, r3
# jump p1
# error
# p1:
# 
# ; no-skip r-i
# if.eq r2, 3
# jump p2
# error
# p2:
# 
# halt

program(0x10b1, 0x20f1, 0x30f1, 0x1212, 0x0010, 0x1193, 0x0010, 0x2312, 0x00a5, 0x0010, 0x2193, 0x00d5, 0x0010, 0x0018)

let i = 0;
while(!(halt | error | (i >= 100)))
  let i = i + 1;
  0 1 0 0
  1 1 x x
end while
0 1 0 1
*/

/* Test case loadstore:
clock run error halt

# #include "../cpudef.asm"
# 
# move r0, 2
# move r1, 5
# 
# ; memory doesn't have 5
# load r2, [r0,0]
# if.eq r2, 5
# error
# 
# ; store and check it does have 5
# store [r0,0], r1
# load r2, [r0,0]
# if.ne r2, 5
# error
# 
# ; check max offset of 31
# move r1, 7
# store [r0,31], r1
# load r2, [r0,31]
# if.ne r2, 7
# error
# 
# ; check base equivalent to offset
# move r2, 0
# add r0, 15
# add r0, 15
# add r0, 1
# load r2, [r0, 0]
# if.ne r2, 7
# error
# 
# halt

program(0x00b1, 0x1171, 0x2006, 0x2293, 0x0010, 0x1007, 0x2006, 0x22a3, 0x0010, 0x11f1, 0x10ff, 0x20fe, 0x23a3, 0x0010, 0x2031, 0x03c1, 0x03c1, 0x0041, 0x2006, 0x23a3, 0x0010, 0x0018)

let i = 0;
while(!(halt | error | (i >= 100)))
  let i = i + 1;
  0 1 0 0
  1 1 x x
end while
0 1 0 1
*/

/* Test case if.ne:
clock run error halt

# #include "../cpudef.asm"
# 
# move r1, 2
# move r2, 3
# move r3, 3
# 
# ; skip r-r
# if.ne r2, r2
# error
# 
# ; skip r-i
# if.ne r1, 2
# error
# 
# ; no-skip r-r
# if.ne r2, r1
# jump p1
# error
# p1:
# 
# ; no-skip r-i
# if.ne r2, 2
# jump p2
# error
# p2:
# 
# halt

program(0x10b1, 0x20f1, 0x30f1, 0x2222, 0x0010, 0x1123, 0x0010, 0x2122, 0x00a5, 0x0010, 0x2123, 0x00d5, 0x0010, 0x0018)

let i = 0;
while(!(halt | error | (i >= 100)))
  let i = i + 1;
  0 1 0 0
  1 1 x x
end while
0 1 0 1
*/
