// Digital circuit vga_blinkenlights.dig as structural Verilog
module vga_blinkenlights (
  input  clock,
  input  [25:0] db,
  input  [15:0] TD,
  input  [7:0] MD,
  output [3:0] R,
  output [3:0] G,
  output [3:0] B,
  output hs,
  output vs,
  output de,
  output [10:0] TA,
  output [9:0] MA
);

  wire error_t, halt_t, immv_t, jump_p13, jump_p14, jump_p15, jump_p16, jump_t, L_p14, L_p15, L_p16, L_p17,
       L_v, PC_p14, PC_p15, PC_p16, PC_p17, R0_p14, R0_p15, R0_p16, R0_p17, R1_p14, R1_p15, R1_p16, R1_p17,
       R_v, rdv_t, res_v, result_p10, result_p11, result_p12, result_p13, rsv_t, skip_p13, skip_p14,
       skip_p15, skip_p16, skip_t, vb, vga_display_1_p23, vga_display_1_p24;
  wire [2:0] aluop_t, cond_t;
  wire [3:0] error_fg_o, halt_p16, L_p4, Op_p14, R2_p17, R3_fg_o, R_fg_o, rd_2_p15, rd_fg_o, rd_t, rs_p15,
       rs_t, vga_display_1_p13;
  wire [4:0] op_t;
  wire [6:0] error_c_o, halt_p15, L_p3, Op_p13, R2_p16, R3_c_o, R_c_o, rd_2_p14, rd_c_o, rs_p14,
       vga_display_1_p12;
  wire [7:0] error_cx_o, error_cy_o, halt_p13, halt_p14, L_p1, L_p2, Op_p11, Op_p12, R2_p14, R2_p15, R3_cx_o,
       R3_cy_o, R_cx_o, R_cy_o, rd_2_p12, rd_2_p13, rd_cx_o, rd_cy_o, rs_p12, rs_p13;
  wire [15:0] debugcopy_1_ctrl, debugcopy_1_decode, imm_t, L_t, PC_t, R0_t, R1_t, R2_t, R3_t, R_t, result_t;

  debugcopy debugcopy_1 (
    .db(db), .clock(clock), .e(vb), .R0(R0_t), .R1(R1_t), .R2(R2_t), .R3(R3_t), .decode(debugcopy_1_decode),
    .ctrl(debugcopy_1_ctrl), .L(L_t), .R(R_t), .result(result_t), .imm(imm_t), .pc(PC_t));
  ctrldec ctrldec_1 (
    .ctrl(debugcopy_1_ctrl), .skip(skip_t), .halt(halt_t), .error(error_t), .jump(jump_t), .aluop(aluop_t),
    .rdvalid(rdv_t), .rsvalid(rsv_t), .immv(immv_t));  // open: stall, mem, store, write, en_fetch, en
  decodedec decodedec_1 (.D(debugcopy_1_decode), .op(op_t), .cond(cond_t), .rs(rs_t), .rd(rd_t));
  // vga_display vga_display_1: pin names not known; wires that end beside it: clock, 12'h280, 12'h10, 12'h60, 12'h30, 1'b1, 12'h1e0, 12'ha, 12'h2, 12'h22, 1'b1, vga_display_1_p12, vga_display_1_p13, 12'h112, TD, MD, R, G, B, hs, vs, de, vga_display_1_p23, vga_display_1_p24, vb, TA, MA
  // vga_labelnum L: pin names not known; wires that end beside it: L_p1, L_p2, L_p3, L_p4, 4'b0010, 4'b0100, 5'b00010, 8'hc, L_v, 7'b0100000, 7'b0111101, 7'b0100000, L_t, L_p14, L_p15, L_p16, L_p17
  // vga_opdisp Op: pin names not known; wires that end beside it: L_p14, L_p15, L_p16, L_p17, 4'b0110, 5'b00001, 8'hb, 1'b1, op_t, cond_t, Op_p11, Op_p12, Op_p13, Op_p14
  // vga_labelnum PC: pin names not known; wires that end beside it: vga_display_1_p23, vga_display_1_p24, {7{1'b0}}, 4'b0000, 4'b0001, 4'b0100, 5'b00001, 8'h8, 1'b1, 7'b0100000, 7'b1010000, 7'b1000011, PC_t, PC_p14, PC_p15, PC_p16, PC_p17
  vga_hex u_R (
    .CX_i(Op_p11), .CY_i(Op_p12), .C_i(Op_p13), .fg_i(Op_p14), .fg_c(4'b0100), .CX_c(6'b000111), .CY_c(8'hc),
    .N(R_t), .en(R_v), .CX_o(R_cx_o), .CY_o(R_cy_o), .C_o(R_c_o), .fg_o(R_fg_o));
  // vga_labelnum R0: pin names not known; wires that end beside it: PC_p14, PC_p15, PC_p16, PC_p17, 4'b0001, 4'b0100, 5'b00011, 8'h2, 1'b1, 7'b0100000, 7'b1010010, 7'b0110000, R0_t, R0_p14, R0_p15, R0_p16, R0_p17
  // vga_hex result: pin names not known; wires that end beside it: R_cx_o, R_cy_o, R_c_o, R_fg_o, 4'b0100, 6'b000011, 8'hc, result_t, res_v, result_p10, result_p11, result_p12, result_p13
  // vga_labelnum R1: pin names not known; wires that end beside it: R0_p14, R0_p15, R0_p16, R0_p17, 4'b0001, 4'b0100, 5'b00011, 8'h3, 1'b1, 7'b0100000, 7'b1010010, 7'b0110001, R1_t, R1_p14, R1_p15, R1_p16, R1_p17
  // vga_string jump: pin names not known; wires that end beside it: result_p10, result_p11, result_p12, result_p13, 4'b0010, 6'b000010, 8'h7, 7'b1001010, 7'b1010101, 7'b1001101, 7'b1010000, jump_t, jump_p13, jump_p14, jump_p15, jump_p16
  // vga_labelnum R2: pin names not known; wires that end beside it: R1_p14, R1_p15, R1_p16, R1_p17, 4'b0001, 4'b0100, 5'b00011, 8'h4, 1'b1, 7'b0100000, 7'b1010010, 7'b0110010, R2_t, R2_p14, R2_p15, R2_p16, R2_p17
  // vga_string skip: pin names not known; wires that end beside it: jump_p13, jump_p14, jump_p15, jump_p16, 4'b0011, 6'b000011, 8'h7, 7'b1010011, 7'b1001011, 7'b1001001, 7'b1010000, skip_t, skip_p13, skip_p14, skip_p15, skip_p16
  vga_labelnum R3 (
    .CX_i(R2_p14), .CY_i(R2_p15), .C_i(R2_p16), .fg_i(R2_p17), .fg_lab(4'b0001), .fg_num(4'b0100),
    .CX_c(5'b00011), .CY_c(8'h5), .en(1'b1), .L_0(7'b0100000), .L_1(7'b1010010), .L_2(7'b0110011), .N(R3_t),
    .CX_o(R3_cx_o), .CY_o(R3_cy_o), .C_o(R3_c_o), .fg_o(R3_fg_o));
  // vga_string halt: pin names not known; wires that end beside it: skip_p13, skip_p14, skip_p15, skip_p16, 4'b0101, 6'b000010, 8'h2, 7'b1001000, 7'b1000001, 7'b1001100, 7'b1010100, halt_t, halt_p13, halt_p14, halt_p15, halt_p16
  vga_regdisp rd (
    .CX_i(R3_cx_o), .CY_i(R3_cy_o), .C_i(R3_c_o), .fg_i(R3_fg_o), .fg_c(4'b0010), .CX_c(6'b000101),
    .CY_c(8'hb), .en(rdv_t), .R(rd_t), .J(jump_t), .sep(7'b0101100), .CX_o(rd_cx_o), .CY_o(rd_cy_o),
    .C_o(rd_c_o), .fg_o(rd_fg_o));
  vga_string error (
    .CX_i(halt_p13), .CY_i(halt_p14), .C_i(halt_p15), .fg_i(halt_p16), .fg_c(4'b0100), .CX_c(6'b000011),
    .CY_c(8'h2), .C_0(7'b1000101), .C_1(7'b1010010), .C_2(7'b1010010), .C_3(7'b1000100), .en(error_t),
    .CX_o(error_cx_o), .CY_o(error_cy_o), .C_o(error_c_o), .fg_o(error_fg_o));
  // vga_regdisp rs: pin names not known; wires that end beside it: rd_cx_o, rd_cy_o, rd_c_o, rd_fg_o, 4'b0010, 6'b000110, 8'hb, rsv_t, rs_t, 1'b0, 7'b0100000, rs_p12, rs_p13, rs_p14, rs_p15
  // vga_regdisp rd_2: pin names not known; wires that end beside it: error_cx_o, error_cy_o, error_c_o, error_fg_o, 4'b0010, 6'b000010, 8'hc, res_v, rd_t, jump_t, 7'b0111101, rd_2_p12, rd_2_p13, rd_2_p14, rd_2_p15
  vga_aluopdisp aluop (
    .CX_i(rs_p12), .CY_i(rs_p13), .C_i(rs_p14), .fg_i(rs_p15), .fg_c(4'b0011), .CX_c(6'b000110), .CY_c(8'hc),
    .en(1'b1), .aop(aluop_t), .CX_o(L_p1), .CY_o(L_p2), .C_o(L_p3), .fg_o(L_p4), .L_v(L_v), .R_v(R_v),
    .res_v(res_v));
  vga_hex result_2 (
    .CX_i(rd_2_p12), .CY_i(rd_2_p13), .C_i(rd_2_p14), .fg_i(rd_2_p15), .fg_c(4'b0100), .CX_c(6'b000111),
    .CY_c(8'hb), .N(imm_t), .en(immv_t), .C_o(vga_display_1_p12), .fg_o(vga_display_1_p13));  // open: CX_o, CY_o

  // Other names for the same wires on the sheet: C = clock

  // Notes on the sheet:
  //   clock: Hz: 2147483647
endmodule
