// Digital circuit vga_frontpanel.dig as structural Verilog
module vga_frontpanel (
  input  clock,
  input  en,
  input  [25:0] db
);

  wire C, vga_blinkenlights_1_p5, vga_blinkenlights_1_p6, vga_blinkenlights_1_p7, vga_blinkenlights_1_p8,
       vga_blinkenlights_1_p9;
  wire [7:0] Map_d, vga_blinkenlights_1_p4;
  wire [9:0] vga_blinkenlights_1_p11;
  wire [10:0] vga_blinkenlights_1_p10;
  wire [15:0] Tile_d, vga_blinkenlights_1_p3;

  and and_1 (C, en, clock);
  // vga_blinkenlights vga_blinkenlights_1: pin names not known; wires that end beside it: C, db, vga_blinkenlights_1_p3, vga_blinkenlights_1_p4, vga_blinkenlights_1_p5, vga_blinkenlights_1_p6, vga_blinkenlights_1_p7, vga_blinkenlights_1_p8, vga_blinkenlights_1_p9, vga_blinkenlights_1_p10, vga_blinkenlights_1_p11
  VGA vga_1 (
    .R(vga_blinkenlights_1_p5), .G(vga_blinkenlights_1_p6), .B(vga_blinkenlights_1_p7),
    .H(vga_blinkenlights_1_p8), .V(vga_blinkenlights_1_p9), .C(C));
  ROM #(.AddrBits(10), .Bits(16)) Tile (.A(vga_blinkenlights_1_p10[9:0]), .sel(1'b1), .D(Tile_d));
  ROM #(.AddrBits(9), .Bits(8)) Map (.A(vga_blinkenlights_1_p11[8:0]), .sel(1'b1), .D(Map_d));
  D_FF #(.Bits(16)) d_ff_1 (.D(Tile_d), .C(C), .Q(vga_blinkenlights_1_p3));  // open: nQ
  D_FF #(.Bits(8)) d_ff_2 (.D(Map_d), .C(C), .Q(vga_blinkenlights_1_p4));  // open: nQ

  // Notes on the sheet:
  //   clock: Hz: 2147483647
  //   contents of Tile (hex, n*v repeats v):
  //   0,0,0,0,0,0,0,0,0,0,4000,d000,d000,d000,d000,d000,0,0,1,7,7,7,7,7,1550,7ff0,7fd0,
  //   1540,0,0,0,0,554,ffd,7fd,154,0,0,0,0,1550,7ff4,fff4,d56d,d07d,d07d,d07d,d07d,0,0,
  //   0,340,740,7d0,1f4,1f4,0,0,0,1c0,1d0,7d0,1f40,1f40,0,0,4000,d1c0,d1d0,d7d0,ef40,ef40,
  //   0,0,1,347,747,7d7,1fb,1fb,d000,d000,d000,4000,4000,d000,d000,d000,7,7,7,1,1,7,7,7,
  //   140,1be4,2ff8,7ffd,7ffd,2ff8,1be4,140,0,140,7d0,1ff4,1ff4,7d0,140,0,d07d,d07d,d56d,
  //   fff4,7ff4,156d,7d,7d,7,7,7,1,0,14,7d,7d,7d,7d,14,0,0,0,0,0,7d,7d,14,0,0,14,7d,7d,
  //   7d00,7d00,1400,0,0,1400,7d00,7d00,fd00,fd00,e950,7ff4,7ff4,e950,fd00,fd00,7f,7f,56b,
  //   1ffd,1ffd,56b,7f,7f,d000,d000,d550,7ff4,7ff4,d550,d000,d000,7,7,557,1ffd,1ffd,557,
  //   7,7,0,0,0,0,0,1400,7d00,7d00,0,0,1550,7ff4,7ff4,1550,0,0,0,0,554,1ffd,1ffd,554,0,
  //   0,d000,d000,d000,d000,d000,4000,0,0,7,7,7,7,7,1,0,0,7d,7d,7d,7d,156d,7ff4,7ff4,1550,
  //   1f4,1f4,7d0,740,154,7fd,ffd,554,1f4,1f4,7d0,740,340,0,0,0,0,0,0,0,154,7fd,ffd,554,
  //   0,0,0,0,1540,7fd0,7ff0,1550,1f40,1f40,7d0,1d0,1c0,0,0,0,ef40,ef40,d7d0,d1d0,d1c0,
  //   4000,0,0,1fb,1fb,7d7,747,347,1,0,0,0,0,0,0,4000,d000,d000,4000,0,0,0,0,1,7,7,1,1550,
  //   7ff4,7ff4,156d,7d,7d,7d,7d,554,1ffd,1ffd,7e54,7f40,7bd0,7af4,7df4,1550,7ff0,ffd0,
  //   d540,d000,d000,d000,d000,554,1ffd,1ffd,7954,7d00,7d00,7d00,7d00,0,0,1d,7d,7d,7d,7d,
  //   7d,0,0,7400,7d00,7d00,7d00,7d00,7d00,7d,7d,7d,14,14,147d,7d7d,7d7d,7d7d,7d7d,7d14,
  //   1400,1400,7d00,7d00,7d00,0,0,1550,7ff4,7ff4,156d,7d,7d,7d00,7d00,7954,1ffd,1ffd,554,
  //   0,0,7d00,7d00,7954,1ffd,1ffd,7954,7d00,7d00,7d,7d,156d,7ff4,7ff4,1550,0,0,0,0,554,
  //   1ffd,1ffd,7954,7d00,7d00,7d,7d,156d,7ff4,7ff4,156d,7d,7d,7d00,7d00,7d00,1400,1400,
  //   7d00,7d00,7d00,d000,d000,d000,4000,0,1400,7d00,7d00,7,7,7,1,0,0,0,0,0,0,0,0,4000,
  //   d000,d000,d000,7d00,7d00,7954,1ffd,1fff,557,7,7,1f7d,1fad,7ed,1fd,15bd,7ff4,7ff4,
  //   1550,7d00,7d00,7d00,7d00,7954,1ffd,1ffd,554,d000,d000,d000,d000,e540,ffd0,7ff0,1550,
  //   7,7,7,7,15b,7ff,ffd,554,7d00,7d00,7d00,7d00,7d00,7400,0,0,1550,7ff4,fff4,e56d,d07d,
  //   d07d,d07d,d07d,554,1ffd,1fff,795b,7d07,7d07,7d07,7d07,1550,7ff0,ffd0,e540,d000,d000,
  //   d000,d000,554,ffd,7ff,15b,7,7,7,7,0,0,1d,7d,1fd,7ed,1fad,1f7d,0,0,7400,7d00,7f40,
  //   7bd0,7af4,7df4,d07d,d07d,d07d,4014,14,7d,7d,7d,7d07,7d07,7957,1fff,1ffd,554,0,0,7d07,
  //   7d07,7957,1ffd,1ffd,7957,7d07,7d07,7d,7d,7d,14,14,7d,7d,7d,7d07,7d07,7d07,1401,1401,
  //   7d07,7d07,7d07,0,0,0,0,14,7d,7d,7d,7d7d,7d7d,147d,14,4014,d07d,d07d,d07d,7d7d,7d7d,
  //   7d14,1400,1401,7d07,7d07,7d07,7d7d,7d7d,147d,14,14,7d,7d,7d,7d00,7d00,7d00,1400,1400,
  //   7d14,7d7d,7d7d,7d,7d,7d,7d,7d,1d,0,0,7d07,7d07,7d07,7d07,795b,1fff,1ffd,554,d07d,
  //   d07d,d07d,d07d,d07d,401d,0,0,7d07,7d07,7d07,7d07,7d07,7401,0,0,7df4,7af4,7bd0,7f40,
  //   7d00,7400,0,0,554,ffd,7fd,154,740,7d0,1f4,1f4,0,0,0,0,0,14,7d,7d,7d00,7d00,7d00,1400,
  //   0,14,7d,7d,7d,7d,7d,14,4014,d07d,d07d,d07d,7d00,7d00,7d00,1400,1401,7d07,7d07,7d07,
  //   7d00,7d00,1400,0,4000,d000,d000,d000,7d,7d,14,0,1,7,7,7,7d00,7d00,1400,0,0,0,0,0,
  //   7df4,7af4,7bd0,7f40,7e54,1ffd,1ffd,554,1f7d,1fad,7ed,1fd,7d,1d,0,0,d07d,d07d,d07d,
  //   d07d,e56d,fff4,7ff4,1550,1f40,1f40,7d0,1d0,1540,7fd0,7ff0,1550
  //   contents of Map (hex, n*v repeats v):
  //   0,0,0,0,0,0,0,0,1,2,a,b,1a,1b,0,0,3,4,0,0,0,0,0,0,0,0,c,0,0,0,0,0,0,0,0,d,0,0,0,0,
  //   0,0,0,0,0,0,0,0,5,2,e,f,1c,1d,0,0,0,6,0,10,0,0,0,0,6,4,11,0,1e,1f,0,0,3,7,0,12,20,
  //   21,0,0,8,9,13,14,22,23,0,0,1,2,15,16,1a,1b,0,0,0,0,17,0,21,0,0,0,0,0,18,19,0,0,0,
  //   0,0,0,0,0,24,25,0,0,0,6,17,10,21,0,0,0,26,27,2c,2d,39,3a,0,0,28,2,a,b,3b,3c,0,0,3,
  //   29,2e,2f,1c,1f,0,0,3,29,18,30,20,3a,0,0,2a,2b,31,30,0,3d,0,0,26,4,31,32,20,3a,0,0,
  //   26,4,33,32,1c,3a,0,0,3,29,0,34,0,3d,0,0,26,29,33,30,1c,3a,0,0,26,29,31,30,20,3a,0,
  //   0,24,25,0,0,24,25,0,0,1,2,35,36,21,0,0,0,0,6,0,11,0,1e,0,0,0,0,18,19,20,1f,0,0,7,
  //   0,12,0,21,0,0,0,3,29,37,38,1a,1b,0,0,3e,3f,44,45,1c,1f,0,0,26,29,33,30,4e,3d,0,0,
  //   40,3f,15,46,3b,4f,0,0,26,4,47,0,1c,1f,0,0,40,3f,a,48,3b,4f,0,0,26,4,33,19,1c,1f,0,
  //   0,26,4,33,19,4e,0,0,0,26,4,47,32,1c,3a,0,0,2a,2b,33,30,4e,3d,0,0,40,41,a,b,3b,3c,
  //   0,0,0,29,49,34,1c,3a,0,0,2a,6,33,11,4e,1e,0,0,2a,0,47,0,1c,1f,0,0,42,43,4a,4b,50,
  //   51,0,0,42,2b,4c,4d,4e,52,0,0,26,29,47,34,1c,3a,0,0,26,29,33,2f,4e,0,0,0,26,29,47,
  //   4d,1c,5b,0,0,26,29,33,55,4e,1e,0,0,26,4,31,32,20,3a,0,0,40,41,a,b,1a,1b,0,0,2a,2b,
  //   47,34,1c,3a,0,0,2a,6,2c,10,5c,0,0,0,2a,2b,56,57,5d,4f,0,0,7,6,12,11,21,1e,0,0,7,6,
  //   58,59,1a,1b,0,0,3,53,17,10,5e,1f,0,0,26,0,47,0,1c,0,0,0,7,0,5a,54,0,1e,0,0,0,29,0,
  //   34,0,3a,0,0,17,54,21,1e,0,0,0,0,0,0,0,0,20,1f
endmodule
